# Fritzing sketch lab1 (saved by Fritzing 0.9.3b)
breadboards: 1

parts:
  R1 = Resistor [tolerance=±5% resistance=330 package=THT]
  LED1 = LED - 5mm [color="Red (633nm)" package="5 mm [THT]"]
  S1 = Pushbutton [package="[THT]"]
  R2 = Resistor [tolerance=±5% resistance=10k package=THT]
  BeagleBone1 = BeagleBone Black

nets:
  N1: R1.Pin_0, BeagleBone1.P8_15_-_GPIO1_15
  N2: R1.Pin_1, LED1.anode
  GND: LED1.cathode, S1.Pin_1, S1.Pin_2, BeagleBone1.P9_1_-_GND
  N3: S1.Pin_3, S1.Pin_4, R2.Pin_1, BeagleBone1.P8_17_-_GPIO0_27
  3.3V: R2.Pin_0, BeagleBone1.P9_4_-_3.3V

custom parts:
  BeagleBone Black: BeagleBone Black rev. A5B
