# Fritzing sketch lab3 (saved by Fritzing 0.9.3b)
breadboards: 1

parts:
  KEYPAD1 = Membrane Matrix Keypad
  BeagleBone1 = BeagleBone Black
  D1 = Rectifier Diode [part_number=1N4148 package="300 mil [THT]"]
  D2 = Rectifier Diode [part_number=1N4148 package="300 mil [THT]"]
  D3 = Rectifier Diode [part_number=1N4148 package="300 mil [THT]"]
  D4 = Rectifier Diode [part_number=1N4148 package="300 mil [THT]"]
  R1 = Resistor [tolerance=±5% resistance=10k package=THT]
  R2 = Resistor [tolerance=±5% resistance=10k package=THT]
  R3 = Resistor [tolerance=±5% resistance=10k package=THT]
  Grove1 = Grove 4 Digit Display

nets:
  N1: KEYPAD1.1, D1.cathode
  N2: KEYPAD1.2, D2.cathode
  N3: KEYPAD1.3, D3.cathode
  N4: KEYPAD1.4, D4.cathode
  N5: KEYPAD1.5, BeagleBone1.P8_22_-_GPIO1_5, R1.Pin_0
  N6: KEYPAD1.6, BeagleBone1.P8_23_-_GPIO1_4, R2.Pin_0
  N7: KEYPAD1.7, BeagleBone1.P8_24_-_GPIO1_1, R3.Pin_0
  GND: BeagleBone1.P9_1_-_GND, BeagleBone1.P9_2_-_GND, R1.Pin_1, R2.Pin_1, R3.Pin_1, Grove1.GND
  3.3V: BeagleBone1.P9_3_-_3.3V, Grove1.VCC
  N8: BeagleBone1.P9_17_-_GPIO0_5/SPI0-CS0(0)/I2C1-SCL(2), Grove1.CLK
  N9: BeagleBone1.P9_18_-_GPIO0_4/SPI0-D1(0)/I2C1-SDA(2), Grove1.DIO
  N10: BeagleBone1.P8_3_-_GPIO1_6, D1.anode
  N11: BeagleBone1.P8_4_-_GPIO1_7, D2.anode
  N12: BeagleBone1.P8_5_-_GPIO1_2, D3.anode
  N13: BeagleBone1.P8_6_-_GPIO1_3, D4.anode

custom parts:
  Membrane Matrix Keypad: Membrane Matrix 3x4 Keypad
  BeagleBone Black: BeagleBone Black rev. A5B
