# Fritzing sketch bbb-rtc (saved by Fritzing 0.9.3b)
breadboards: 1

parts:
  Part1 = Tiny RTC - DS1307 Breakout Board
  BeagleBone1 = BeagleBone Black

nets:
  N1: Part1.SCL, BeagleBone1.P9_19_-_GPIO0_15/I2C2-SCL(3)/SPI1-CS1(4)
  N2: Part1.SDA, BeagleBone1.P9_20_-_GPIO0_14/I2C2-SDA(3)/SPI1-CS0(4)
  N3: Part1.VCC, BeagleBone1.P9_7_-_5V
  N4: Part1.GND, BeagleBone1.P9_1_-_GND

custom parts:
  Tiny RTC - DS1307 Breakout Board: The Tiny RTC is a breakout board for the Dallas Semiconductor/Maxim Integrated DS1307 real-time clock. The DS1307 counts seconds, minutes, hours, date of the month, month, day of the week, and year (with compensation for leap-years). The breakout board also has space for a DS18B20 digital thermometer.
  BeagleBone Black: BeagleBone Black rev. A5B
